// Logisim project 2_mux8_1.vhd.circ as structural Verilog
module main (
  input  d0,
  input  d1,
  input  d2,
  input  d3,
  input  d4,
  input  d5,
  input  d6,
  input  d7,
  input  [2:0] ch,
  output data
);

  mux8_1 mux8_1_1 (.d0(d0), .d1(d1), .d2(d2), .d3(d3), .d4(d4), .d5(d5), .d6(d6), .d7(d7), .ch(ch), .data(data));
endmodule

// VHDL entity mux8_1, as the project stores it:
-- Library and package
library ieee;
use ieee.std_logic_1164.all;
use ieee.std_logic_arith.all;
use ieee.std_logic_unsigned.all;

-- entity
entity mux8_1 is
    port(
        d0, d1, d2, d3, d4, d5, d6, d7 : in std_logic;
        ch   : in std_logic_vector(2 downto 0);
        data : out std_logic
    );
end entity mux8_1;

-- architecture
architecture bhv of mux8_1 is
begin
    process(d0, d1, d2, d3, d4, d5, d6, d7, ch)
    begin
        case ch is
            when "000" => data <= d0;
            when "001" => data <= d1;
            when "010" => data <= d2;
            when "011" => data <= d3;
            when "100" => data <= d4;
            when "101" => data <= d5;
            when "110" => data <= d6;
            when "111" => data <= d7;
            when others => data <= '0';
        end case;
    end process;
end architecture bhv;
