// Logisim project 4.vote25.circ as structural Verilog
module main (
  input  [24:0] in_1,
  output out_2
);

  vote25 vote25_1 (.vt(in_1), .result(out_2));
endmodule

// VHDL entity vote25, as the project stores it:
-- Library and package
library ieee;
use ieee.std_logic_1164.all;
use ieee.std_logic_arith.all;
use ieee.std_logic_unsigned.all;

-- entity
entity vote25 is
    port(
        vt     : in std_logic_vector(25 downto 1);
        result : out std_logic
    );
end entity vote25;

-- architecture
architecture bhv of vote25 is
begin
    process(vt)
        variable sum : integer range 0 to 25;
    begin
        sum := 0;
        for i in 1 to 25 loop
            if (vt(i) = '1') then
                sum := sum + 1;
            end if;
        end loop;

        if sum >= 13 then
            result <= '1';
        else
            result <= '0';
        end if;
    end process;
end architecture bhv;
