// Logisim project 5.cnt13_seg.circ as structural Verilog
module main (
  input  in_1,
  input  [12:0] in_2
);

  wire [7:0] cnt13_seg_1_display;

  cnt13_seg cnt13_seg_1 (.en(in_1), .vt(in_2), .display(cnt13_seg_1_display));
  _7_Segment_Display u_7_segment_display_1 (
    .g(cnt13_seg_1_display[1]), .f(cnt13_seg_1_display[2]), .a(cnt13_seg_1_display[7]),
    .b(cnt13_seg_1_display[6]), .e(cnt13_seg_1_display[3]), .d(cnt13_seg_1_display[4]),
    .c(cnt13_seg_1_display[5]), .dp(cnt13_seg_1_display[0]));
endmodule

// VHDL entity cnt13_seg, as the project stores it:
-- Library and package
library ieee;
use ieee.std_logic_1164.all;
use ieee.std_logic_arith.all;
use ieee.std_logic_unsigned.all;

-- entity
entity cnt13_seg is
    port(
        en      : in std_logic;
        vt      : in std_logic_vector(12 downto 0); -- 13-bit vector
        display : out std_logic_vector(7 downto 0)  -- "abcdefgdp"
    );
end entity cnt13_seg;

-- architecture
architecture bhv of cnt13_seg is
begin
    process(en, vt)
        variable sum : integer range 0 to 15;
    begin
        -- 1. Count the number of '1's in vt
        sum := 0;
        for i in 0 to 12 loop
            if (vt(i) = '1') then
                sum := sum + 1;
            end if;
        end loop;

        -- 2. Display on 7-segment with enable control
        if en = '0' then
            display <= "00000000";
        else
            case sum is
                -- Digits 0 to 9
                when 0  => display <= "11111100"; -- 0
                when 1  => display <= "01100000"; -- 1
                when 2  => display <= "11011010"; -- 2
                when 3  => display <= "11110010"; -- 3
                when 4  => display <= "01100110"; -- 4
                when 5  => display <= "10110110"; -- 5
                when 7  => display <= "11100000"; -- 7
                when 8  => display <= "11111110"; -- 8
                when 9  => display <= "11100110"; -- 9
                -- Letters A to F (10 to 15)
                when 10 => display <= "11101110"; -- A
                when 11 => display <= "00111110"; -- b
                when 12 => display <= "10011100"; -- C
                when 13 => display <= "01111010"; -- d
                when 14 => display <= "10011110"; -- E
                when 15 => display <= "10001110"; -- F
                when others => display <= "00000000";
            end case;
        end if;
    end process;
end architecture bhv;

// VHDL entity seg_letters, as the project stores it:
-- Library and package
library ieee;
use ieee.std_logic_1164.all;
use ieee.std_logic_arith.all;
use ieee.std_logic_unsigned.all;

-- entity
entity seg_letters is
    port(
        en      : in std_logic;
        dat     : in std_logic_vector(2 downto 0);
        display : out std_logic_vector(7 downto 0)
    );
end entity seg_letters;

-- architecture
architecture bhv of seg_letters is
begin
    process(en, dat)
    begin
        if en = '0' then
            display <= "00000000";
        else
            case dat is
                when "000" => display <= "11101110"; -- a (A)
                when "001" => display <= "00111110"; -- b
                when "010" => display <= "10011100"; -- c (C)
                when "011" => display <= "01111010"; -- d
                when "100" => display <= "10001110"; -- f (F)
                when "101" => display <= "11110110"; -- g
                when others => display <= "00000000";
            end case;
        end if;
    end process;
end architecture bhv;
