// Logisim project and_or_circ.circ as structural Verilog
module main (
  input  in_1,
  input  in_2,
  input  in_3,
  input  in_4,
  output out_5,
  output out_6
);

  and_or and_or_1 (.a(in_1), .b(in_2), .c(in_3), .d(in_4), .out1(out_5), .out2(out_6));
endmodule

// VHDL entity and_or, as the project stores it:
LIBRARY ieee;
USE ieee.std_logic_1164.all;
use ieee.std_logic_arith.all;
use ieee.std_logic_unsigned.all;

ENTITY and_or IS
  PORT (
    a, b, c, d      : IN  std_logic;
    out1, out2		: OUT std_logic
    );
END and_or;

ARCHITECTURE bhv OF and_or IS

BEGIN
	
  out1 <= a and b and c and d;
	out2 <= a or b or c or d;

END bhv;
